// Digital circuit LeTecMat.dig as structural Verilog
module LeTecMat (
  input  clk,
  input  clk_2,
  output C
);

  wire _0_a, _4_a, _8_a, _10_a, _10_b, _11_b, _12_b, _13_b, _14_a, _18_a, C_2_a, C_a, d_ff_1_q, jk_ff_1_q,
       jk_ff_2_q, jk_ff_as_1_q, letecmat4x4_1_kp, nand_1_out, nand_2_out, nand_3_out, not_1_out, not_2_out,
       pullup_1_out, pullup_2_out, pullup_3_out, pullup_4_out;
  wire [3:0] d_ff_2_q, letecmat4x4_1_q0;

  // Probe L1 on _0_a
  // Probe L2 on _4_a
  // Probe L3 on _8_a
  // Probe L4 on C_a
  PullUp pullup_1 (.out(pullup_1_out));
  PullUp pullup_2 (.out(pullup_2_out));
  Switch _0 (.A(_0_a), .B(pullup_2_out));
  Switch _4 (.A(_4_a), .B(pullup_2_out));
  Switch _8 (.A(_8_a), .B(pullup_2_out));
  Switch u_C (.A(C_a), .B(pullup_2_out));
  PullUp pullup_3 (.out(pullup_3_out));
  PullUp pullup_4 (.out(pullup_4_out));
  Switch _10 (.A(_10_a), .B(_10_b));
  Switch _14 (.A(_14_a), .B(_10_b));
  Switch _18 (.A(_18_a), .B(_10_b));
  Switch C_2 (.A(C_2_a), .B(_10_b));
  Switch _1 (.A(_0_a), .B(pullup_1_out));
  Switch _5 (.A(_4_a), .B(pullup_1_out));
  Switch _9 (.A(_8_a), .B(pullup_1_out));
  Switch D (.A(C_a), .B(pullup_1_out));
  Switch _11 (.A(_10_a), .B(_11_b));
  Switch _15 (.A(_14_a), .B(_11_b));
  Switch _19 (.A(_18_a), .B(_11_b));
  Switch D_2 (.A(C_2_a), .B(_11_b));
  PullDown pulldown_1 (.out(_10_b));
  Switch _2 (.A(_0_a), .B(pullup_3_out));
  Switch _6 (.A(_4_a), .B(pullup_3_out));
  Switch A (.A(_8_a), .B(pullup_3_out));
  Switch E (.A(C_a), .B(pullup_3_out));
  Switch _12 (.A(_10_a), .B(_12_b));
  Switch _16 (.A(_14_a), .B(_12_b));
  Switch A_2 (.A(_18_a), .B(_12_b));
  Switch E_2 (.A(C_2_a), .B(_12_b));
  PullDown pulldown_2 (.out(_11_b));
  Switch _3 (.A(_0_a), .B(pullup_4_out));
  Switch _7 (.A(_4_a), .B(pullup_4_out));
  Switch B (.A(_8_a), .B(pullup_4_out));
  Switch F (.A(C_a), .B(pullup_4_out));
  Switch _13 (.A(_10_a), .B(_13_b));
  Switch _17 (.A(_14_a), .B(_13_b));
  Switch B_2 (.A(_18_a), .B(_13_b));
  Switch F_2 (.A(C_2_a), .B(_13_b));
  PullDown pulldown_3 (.out(_12_b));
  PullDown pulldown_4 (.out(_13_b));
  nand nand_1 (nand_1_out, pullup_1_out, pullup_4_out);
  nand nand_2 (nand_2_out, pullup_3_out, pullup_4_out);
  nand nand_3 (nand_3_out, pullup_4_out, pullup_3_out, pullup_1_out, pullup_2_out);
  JK_FF jk_ff_1 (.J(1'b1), .C(clk), .K(1'b1), .Q(jk_ff_1_q));  // open: nQ
  nand nand_4 (_0_a, not_2_out, not_1_out);
  nand nand_5 (_4_a, not_2_out, jk_ff_1_q);
  nand nand_6 (_8_a, jk_ff_2_q, not_1_out);
  nand nand_7 (C_a, jk_ff_2_q, jk_ff_1_q);
  LeTecMat4x4 letecmat4x4_1 (
    .clk(clk_2), .L0(_10_a), .L1(_14_a), .L2(_18_a), .L3(C_2_a), .C0(_10_b), .C1(_11_b), .C2(_12_b),
    .C3(_13_b), .Q0(letecmat4x4_1_q0[0]), .Q1(letecmat4x4_1_q0[1]), .Q2(letecmat4x4_1_q0[2]),
    .Q3(letecmat4x4_1_q0[3]), .Kp(letecmat4x4_1_kp));
  not not_1 (not_1_out, jk_ff_1_q);
  JK_FF_AS jk_ff_as_1 (.Set(nand_3_out), .J(1'b0), .C(C_a), .K(1'b1), .Clr(1'b0), .Q(jk_ff_as_1_q));  // open: nQ
  JK_FF jk_ff_2 (.J(jk_ff_1_q), .C(clk), .K(jk_ff_1_q), .Q(jk_ff_2_q));  // open: nQ
  not not_2 (not_2_out, jk_ff_2_q);
  D_FF d_ff_1 (.D(jk_ff_as_1_q), .C(C_a), .Q(d_ff_1_q));  // open: nQ
  or or_1 (C, jk_ff_as_1_q, d_ff_1_q);
  D_FF d_ff_2 (.D(nand_1_out), .C(C), .Q(d_ff_2_q[0]));  // open: nQ
  D_FF d_ff_3 (.D(nand_2_out), .C(C), .Q(d_ff_2_q[1]));  // open: nQ
  D_FF d_ff_4 (.D(jk_ff_1_q), .C(C), .Q(d_ff_2_q[2]));  // open: nQ
  D_FF d_ff_5 (.D(jk_ff_2_q), .C(C), .Q(d_ff_2_q[3]));  // open: nQ
  Seven_Seg_Hex seven_seg_hex_1 (.d(letecmat4x4_1_q0), .dp(letecmat4x4_1_kp));
  Seven_Seg_Hex seven_seg_hex_2 (.d(d_ff_2_q), .dp(1'b0));

  // Notes on the sheet:
  //   clk: Hz: 30
  //   clk_2: Hz: 30
endmodule
