// Digital circuit LeTecMat4x4.dig as structural Verilog
module LeTecMat4x4 (
  input  clk,
  input  C0,
  input  C1,
  input  C2,
  input  C3,
  output Q0,
  output Q1,
  output Q2,
  output Q3,
  output L0,
  output L1,
  output L2,
  output L3,
  output Kp
);

  wire and_5_out, d_ff_as_1_q, jk_ff_1_q, jk_ff_2_q, not_1_out, not_2_out, not_3_out, or_1_out, or_2_out,
       or_3_out;
  wire [3:0] d_ff_1_q;

  or or_1 (or_1_out, C1, C3);
  or or_2 (or_2_out, C2, C3);
  or or_3 (or_3_out, C3, C2, C1, C0);
  JK_FF jk_ff_1 (.J(1'b1), .C(clk), .K(1'b1), .Q(jk_ff_1_q));  // open: nQ
  and and_1 (L0, not_3_out, not_1_out);
  and and_2 (L1, not_3_out, jk_ff_1_q);
  and and_3 (L2, jk_ff_2_q, not_1_out);
  and and_4 (L3, jk_ff_2_q, jk_ff_1_q);
  not not_1 (not_1_out, jk_ff_1_q);
  not not_2 (not_2_out, clk);
  JK_FF jk_ff_2 (.J(jk_ff_1_q), .C(clk), .K(jk_ff_1_q), .Q(jk_ff_2_q));  // open: nQ
  not not_3 (not_3_out, jk_ff_2_q);
  and and_5 (and_5_out, not_2_out, or_3_out);
  D_FF_AS d_ff_as_1 (.Set(or_3_out), .D(1'b0), .C(~L3), .Clr(1'b0), .Q(d_ff_as_1_q));  // open: nQ
  D_FF d_ff_1 (.D(or_1_out), .C(and_5_out), .Q(d_ff_1_q[0]));  // open: nQ
  D_FF d_ff_2 (.D(or_2_out), .C(and_5_out), .Q(d_ff_1_q[1]));  // open: nQ
  D_FF d_ff_3 (.D(jk_ff_1_q), .C(and_5_out), .Q(d_ff_1_q[2]));  // open: nQ
  D_FF d_ff_4 (.D(jk_ff_2_q), .C(and_5_out), .Q(d_ff_1_q[3]));  // open: nQ
  D_FF d_ff_5 (.D(d_ff_as_1_q), .C(~L3), .Q(Kp));  // open: nQ
  ROM #(.AddrBits(4), .Bits(4)) m (.A(d_ff_1_q), .sel(1'b1), .D({Q3, Q2, Q1, Q0}));

  // Notes on the sheet:
  //   clk: Hz: 2
  //   contents of m (hex, n*v repeats v):
  //   1,2,3,a,4,5,6,b,7,8,9,c,e,0,f,d
endmodule
