// Digital circuit Senha1.dig as structural Verilog
module Senha1 (
  input  clk
);

  wire _0_a, _0_b, _1_b, _2_b, _3_b, _4_a, _8_a, C_a, letecmat4x4_1_kp;
  wire [3:0] d_ff_1_q, d_ff_2_q, d_ff_3_q, d_ff_4_q, letecmat4x4_1_q0;

  Switch _0 (.A(_0_a), .B(_0_b));
  Switch _4 (.A(_4_a), .B(_0_b));
  Switch _8 (.A(_8_a), .B(_0_b));
  Switch C (.A(C_a), .B(_0_b));
  Switch _1 (.A(_0_a), .B(_1_b));
  Switch _5 (.A(_4_a), .B(_1_b));
  Switch _9 (.A(_8_a), .B(_1_b));
  Switch D (.A(C_a), .B(_1_b));
  PullDown pulldown_1 (.out(_0_b));
  Switch _2 (.A(_0_a), .B(_2_b));
  Switch _6 (.A(_4_a), .B(_2_b));
  Switch A (.A(_8_a), .B(_2_b));
  Switch E (.A(C_a), .B(_2_b));
  PullDown pulldown_2 (.out(_1_b));
  Switch _3 (.A(_0_a), .B(_3_b));
  Switch _7 (.A(_4_a), .B(_3_b));
  Switch B (.A(_8_a), .B(_3_b));
  Switch F (.A(C_a), .B(_3_b));
  PullDown pulldown_3 (.out(_2_b));
  PullDown pulldown_4 (.out(_3_b));
  LeTecMat4x4 letecmat4x4_1 (
    .clk(clk), .L0(_0_a), .L1(_4_a), .L2(_8_a), .L3(C_a), .C0(_0_b), .C1(_1_b), .C2(_2_b), .C3(_3_b),
    .Q0(letecmat4x4_1_q0[0]), .Q1(letecmat4x4_1_q0[1]), .Q2(letecmat4x4_1_q0[2]), .Q3(letecmat4x4_1_q0[3]),
    .Kp(letecmat4x4_1_kp));
  Seven_Seg_Hex seven_seg_hex_1 (.d(d_ff_1_q), .dp(1'b0));
  D_FF #(.Bits(4)) d_ff_1 (.D(letecmat4x4_1_q0), .C(letecmat4x4_1_kp), .Q(d_ff_1_q));  // open: nQ
  D_FF #(.Bits(4)) d_ff_2 (.D(letecmat4x4_1_q0), .C(letecmat4x4_1_kp), .Q(d_ff_2_q));  // open: nQ
  Seven_Seg_Hex seven_seg_hex_2 (.d(d_ff_2_q), .dp(1'b0));
  D_FF #(.Bits(4)) d_ff_3 (.D(letecmat4x4_1_q0), .C(letecmat4x4_1_kp), .Q(d_ff_3_q));  // open: nQ
  Seven_Seg_Hex seven_seg_hex_3 (.d(d_ff_3_q), .dp(1'b0));
  Seven_Seg_Hex seven_seg_hex_4 (.d(d_ff_4_q), .dp(1'b0));
  D_FF #(.Bits(4)) d_ff_4 (.D(letecmat4x4_1_q0), .C(letecmat4x4_1_kp), .Q(d_ff_4_q));  // open: nQ

  // Notes on the sheet:
  //   clk: Hz: 10
endmodule
