// Digital circuit TetTecMatCPLD.dig as structural Verilog
module TetTecMatCPLD (
  input  CLK50,
  input  C0,
  input  C1,
  input  C2,
  input  C3,
  output a,
  output b,
  output c,
  output d,
  output e,
  output f,
  output g,
  output L1,
  output L2,
  output L3,
  output L4,
  output KP
);

  wire div8ff_1_clk_out;
  wire [3:0] letecmat4x4_1_q0;

  Div8FF div8ff_1 (.CLK_in(CLK50), .CLK_out(div8ff_1_clk_out));
  LeTecMat4x4 letecmat4x4_1 (
    .clk(div8ff_1_clk_out), .L0(L1), .L1(L2), .L2(L3), .L3(L4), .C0(C0), .C1(C1), .C2(C2), .C3(C3),
    .Q0(letecmat4x4_1_q0[0]), .Q1(letecmat4x4_1_q0[1]), .Q2(letecmat4x4_1_q0[2]), .Q3(letecmat4x4_1_q0[3]),
    .Kp(KP));
  decodificador7segmentos decodificador7segmentos_1 (
    .d0(letecmat4x4_1_q0[0]), .d1(letecmat4x4_1_q0[1]), .d2(letecmat4x4_1_q0[2]), .d3(letecmat4x4_1_q0[3]),
    .a(a), .b(b), .c(c), .d(d), .e(e), .f(f), .g(g));
endmodule
